// Logisim project CU.circ as structural Verilog: 2 circuits, main circuit main
// CU
module main (
  input  [15:0] Instruction,
  output [3:0] COM,
  output [2:0] A1,
  output [2:0] A2,
  output [7:0] MA,
  output [2:0] A_Input,
  output S_L,
  output MOV
);

  wire and_2_out, and_3_out, not_1_out, or_1_out;

  PARSER parser_1 (.Instruction(Instruction), .COMMAND(COM), .A1(A1), .A2(A2), .M1(MA));
  and and_1 (MOV, ~COM[3], ~COM[2], ~COM[1], ~COM[0]);  // AND_Gate
  and and_2 (and_2_out, COM[0], ~COM[1], ~COM[2], ~COM[3]);  // AND_Gate
  or or_1 (or_1_out, and_2_out, and_3_out);
  and and_3 (and_3_out, ~COM[0], COM[1], ~COM[2], ~COM[3]);  // AND_Gate
  Multiplexer #(.width(3)) multiplexer_1 (.in0(A2), .in1(3'b000), .out(A_Input), .sel(or_1_out));  // open: en
  not not_1 (not_1_out, and_2_out);
  and and_4 (S_L, and_3_out, not_1_out);
endmodule

// PAR
module PARSER (
  input  [15:0] Instruction,
  output [3:0] COMMAND,
  output [2:0] A1,
  output [2:0] A2,
  output [7:0] M1
);


  assign A1 = Instruction[6:4];
  assign A2 = Instruction[9:7];
  assign COMMAND = Instruction[3:0];
  assign M1 = Instruction[11:4];
endmodule
