// Logisim project procesor.circ as structural Verilog
module Procesor (
  input  [15:0] I_Input,
  input  LD,
  input  [15:0] in_3,
  output [15:0] I_Output,
  output [7:0] ALU_Output,
  output [7:0] out_6,
  output [2:0] out_7
);

  wire CLK_out, main_1_p3, main_1_p4, main_1_p5, not_1_out;
  wire [2:0] main_1_p7, main_1_p8;
  wire [3:0] main_1_p6;
  wire [7:0] MEM, multiplexer_1_out, ram_2_data, registers_1_value1, registers_1_value2;

  Clock CLK (.out(CLK_out));
  Multiplexer #(.width(8)) multiplexer_1 (
    .in0(ALU_Output), .in1(ram_2_data), .out(multiplexer_1_out), .sel(main_1_p5));  // open: en
  // CU_main main_1: pin names not known; wires that end beside it: in_3, MEM, main_1_p3, main_1_p4, main_1_p5, main_1_p6, main_1_p7, main_1_p8, out_7
  not not_1 (not_1_out, main_1_p4);
  RAM #(.dataWidth(16), .bus("separate")) ram_1 (
    .din(I_Input), .data(I_Output), .clk(CLK_out), .ld(LD));  // open: addr, str, sel, clr
  Registers registers_1 (
    .DESTINATION(main_1_p8), .VALUE1(registers_1_value1), .CLK(CLK_out), .SOURCE1(main_1_p7),
    .in_7(not_1_out), .MEM(multiplexer_1_out), .VALUE2(registers_1_value2), .SOURCE2(out_7), .AX(out_6),
    .in_2(main_1_p3));
  RAM #(.bus("separate")) ram_2 (
    .addr(MEM), .din(out_6), .data(ram_2_data), .str(main_1_p4), .clk(CLK_out), .ld(not_1_out));  // open: sel, clr
  ALU alu_1 (
    .R1__Value_of_first_register(registers_1_value1), .R2__Value_of_second_register(registers_1_value2),
    .OUT__ALU_output(ALU_Output), .COM__Value_of_command__0000_to_1111(main_1_p6));  // open: FLAGS_ZCOP

  // Other names for the same wires on the sheet: AX[7:0] = out_6

  // Notes on the sheet:
  //   Instruction
  //   Memory Adress
  //   1
  //   2
  //   INSTRUCTIONS
  //   5,6,7
  //   DATA
  //   3
  //   3
  //   4
  //   ALU_Value
  //   3. Value of first adress 
  //   4. Value of second adress
  //   5. First adress
  //   6. Second adress
  //   7. Input adress
  //   1. bit(value = is this instruction MOV)
  //   2. bit(value = is this instruction LOAD or STORE)
endmodule
